# Fritzing sketch killswitch (saved by Fritzing 0.9.3b)
perfboards: 1

parts:
  Raspberry_Pi_1 = Raspberry Pi 3 [part_number=RPI-3-V1.2]
  S1 = Round Pushbutton
  LED1 = RGB LED (com. cathode, rgb) [package="5 mm [THT]"]
  J3 = female pin header, 6 pins [form="♀ (female)"]
  R3 = Resistor [tolerance=±5% resistance=10k package=THT]
  R4 = Resistor [tolerance=±5% resistance=10k package=THT]
  J1 = female pin header, 8 pins [form="♀ (female)"]
  J2 = female pin header, 3 pins [form="♀ (female)"]

nets:
  N1: Raspberry_Pi_1.3v3, S1.leg0
  N2: Raspberry_Pi_1.GND, LED1.common_cathode, R3.Pin_0
  N3: Raspberry_Pi_1.GIPO17, LED1.red_anode
  N4: Raspberry_Pi_1.GIPO27, LED1.green_anode
  N5: Raspberry_Pi_1.GIPO22, LED1.blue_anode
  N6: Raspberry_Pi_1.GIPO15, S1.leg1, R3.Pin_1
  N7: J3.pin1, J1.pin1
  N8: J3.pin2, R4.Pin_1, J2.pin3
  N9: J3.pin3, J1.pin5
  N10: J3.pin4, J1.pin6
  N11: J3.pin5, J1.pin7
  N12: J3.pin6, J1.pin8
  N13: R4.Pin_0, J2.pin1

notes:
  3V3
  GPIO
  GND
  B
  G
  R
